# Fritzing sketch Circuito_Dettagliato (saved by Fritzing 0.8.7b)
breadboards: 1

parts:
  U1 = ESP32-38PinWide [part_number=ESP32-38PinWide]
  OLED1 = OLED 128x64 I2C Monochrome Display
  ZS-042_RTC1 = ZS-042 RTC Module
  sdCard1 = my_sdCard
  Bottone_2 = Pushbutton [package="[SMD]"]
  Bottone_1 = Pushbutton [package="[SMD]"]
  RF-NANO = Arduino Nano (Rev3.0)
  10Kohm = Resistor [tolerance=±5% resistance=220 package=THT]
  10Kohm1 = Resistor [tolerance=±5% resistance=220 package=THT]

nets:
  VDD: U1.3.3, U1.GPIO26, U1.GPIO14, U1.GPIO15, OLED1.VDD, ZS-042_RTC1.VCC, Bottone_2.Pin_1, Bottone_2.Pin_2, Bottone_1.Pin_1, Bottone_1.Pin_2, 10Kohm.Pin_0, 10Kohm1.Pin_0
  N1: U1.GPIO25, U1.GPIO2, RF-NANO.D4
  GND: U1.GND, OLED1.GND, ZS-042_RTC1.GND, sdCard1.GND, RF-NANO.GND, 10Kohm.Pin_1, 10Kohm1.Pin_1
  VIN: U1.VIN, sdCard1.VCC, RF-NANO.VIN
  N2: U1.GPIO5, sdCard1.CS
  N3: U1.GPIO18, sdCard1.SCK
  N4: U1.GPIO19, sdCard1.MISO
  N5: U1.GPIO21, OLED1.SCK, ZS-042_RTC1.SCL
  N6: U1.GPIO22, OLED1.SDA, ZS-042_RTC1.SDA
  N7: U1.GPIO23, sdCard1.MOSI

notes:
  1.GND
  2.VCC
  3.MISO
  4.MOSI
  5.SCK
  6.CS

custom parts:
  ESP32-38PinWide: Generic 38-Pin ESP32 with wide format (only access to one side of pins on a breadboard) based on Stephen Lilley's HiLetgo ESP-WROOM-32 ESP32 ESP-32S Development Board.
  my_sdCard: micro sdCard Adapter with 90º pin header. Use a filtering Capacitor between CS and GND if needed. PCB View Pinouts are Reversed for laying parallel on PCB using a 90º pin header.
