# Fritzing sketch Circuito_Semplice (saved by Fritzing 0.8.7b)
breadboards: 1

parts:
  ESP32 = ESP32-38PinWide [part_number=ESP32-38PinWide]
  RF-NANO = Arduino Nano (Rev3.0)
  Display_OLED_0_96" = OLED 128x64 I2C Monochrome Display
  S1 = Pushbutton [package="[THT]"]
  S2 = Pushbutton [package="[THT]"]
  MicroSD_Card_Adapter = SD Card Module
  RTC = ZS-042 RTC Module  # not connected
  10K = Resistor [package="2010 [SMD]"]
  10K_2 = Resistor [package="2010 [SMD]"]

nets:
  N1: ESP32.3.3, Display_OLED_0_96".VDD, S1.Pin_1, S1.Pin_2, S2.Pin_1, S2.Pin_2
  N2: ESP32.GPIO25, ESP32.GPIO2, RF-NANO.D4
  N3: ESP32.GPIO26, S2.Pin_3, S2.Pin_4, 10K_2.Pin_0
  N4: ESP32.GPIO14, ESP32.GPIO15, S1.Pin_3, S1.Pin_4, 10K.Pin_0
  GND: ESP32.GND, Display_OLED_0_96".GND, MicroSD_Card_Adapter.GND#0, 10K.Pin_1, 10K_2.Pin_1
  N5: ESP32.VIN, MicroSD_Card_Adapter.+5
  N6: ESP32.GPIO5, MicroSD_Card_Adapter.CS
  N7: ESP32.GPIO18, MicroSD_Card_Adapter.SCK
  N8: ESP32.GPIO19, MicroSD_Card_Adapter.MISO
  N9: ESP32.GPIO21, Display_OLED_0_96".SCK
  N10: ESP32.GPIO22, Display_OLED_0_96".SDA
  N11: ESP32.GPIO23, MicroSD_Card_Adapter.MOSI

custom parts:
  ESP32-38PinWide: Generic 38-Pin ESP32 with wide format (only access to one side of pins on a breadboard) based on Stephen Lilley's HiLetgo ESP-WROOM-32 ESP32 ESP-32S Development Board.
  SD Card Module: SD Card Module Slot Socket Reader For Arduino ARM MCU
